# Fritzing sketch shema (saved by Fritzing 0.9.2b)

parts:
  Composant1 = Arduino Uno (Rev3) - ICSP
  M1 = DC Motor
  Composant2 = Arduino Motor Shield
  M2 = DC Motor

nets:
  N1: Composant1.D2, Composant2.D12
  N2: Composant1.D3_PWM, Composant2.D3
  N3: Composant1.D4, Composant2.D13
  N4: Composant1.D5_PWM, Composant2.D11
  N5: M1.pin_1, Composant2.OUT4
  N6: M1.pin_2, Composant2.OUT3
  N7: Composant2.OUT2, M2.pin_1
  N8: Composant2.OUT1, M2.pin_2
